# Fritzing sketch artu (saved by Fritzing 0.9.3b)

parts:
  Part1 = Arduino Nano (Rev3.0)
  S1 = Round Pushbutton
  S2 = Round Pushbutton
  U1 = L9110 H-bridge module [part_number="L9110 H-bridge"]
  M1 = DC Motor
  S3 = Taiway 100-SP-X-T1 SPDT Miniature Toggle Switch [part_number=100-SP-X-T1-0-0-B1-M1 package=THT]
  U2 = LIPO-2000mAh [package=lipo-2000]
  M2 = RioRand LM2596

nets:
  N1: Part1.D7, S2.leg1
  N2: Part1.D8, S2.leg0
  N3: Part1.D9, S1.leg1
  N4: Part1.D10, U1.B-IA
  N5: Part1.D11/MOSI, U1.B-IB
  N6: Part1.D12/MISO, S1.leg0
  N7: Part1.GND, U2.-
  N8: U1.GND, M2.Pin_4
  N9: U1.VCC, M2.Pin_3
  N10: U1.MOTOR_B-A, M1.pin_2
  N11: U1.MOTOR_B-B, M1.pin_1
  N12: S3.COM, U2.+
  N13: S3.L2, M2.Pin_1
